// Logisim project 1bit adder.circ as structural Verilog: 2 circuits, main circuit main
module main (
  input  in_1,
  input  in_2,
  input  in_3,
  input  in_4,
  input  in_5,
  input  in_6,
  input  in_7,
  input  in_8,
  input  in_9,
  input  in_10,
  input  in_11,
  input  in_12,
  input  in_13,
  input  in_14,
  input  in_15,
  input  in_16,
  input  [7:0] in_17,
  input  [7:0] in_18,
  output out_19,
  output out_20,
  output out_21,
  output out_22,
  output out_23,
  output out_24,
  output out_25,
  output out_26,
  output [7:0] out_27,
  output out_28,
  output out_29
);

  wire basic_1_cout, basic_2_cout, basic_3_cout, basic_4_cout, basic_5_cout, basic_6_cout, basic_7_cout;

  Basic basic_1 (.Cin(1'b0), .X(in_1), .Y(in_2), .S(out_19), .Cout(basic_1_cout));
  Basic basic_2 (.Cin(basic_1_cout), .X(in_3), .Y(in_4), .S(out_20), .Cout(basic_2_cout));
  Adder adder_1 (.a(in_17), .b(in_18), .out(out_27), .cin(1'b0), .cout(out_28));
  Basic basic_3 (.Cin(basic_2_cout), .X(in_5), .Y(in_6), .S(out_21), .Cout(basic_3_cout));
  Basic basic_4 (.Cin(basic_3_cout), .X(in_7), .Y(in_8), .S(out_22), .Cout(basic_4_cout));
  Basic basic_5 (.Cin(basic_4_cout), .X(in_9), .Y(in_10), .S(out_23), .Cout(basic_5_cout));
  Basic basic_6 (.Cin(basic_5_cout), .X(in_11), .Y(in_12), .S(out_24), .Cout(basic_6_cout));
  Basic basic_7 (.Cin(basic_6_cout), .X(in_13), .Y(in_14), .S(out_25), .Cout(basic_7_cout));
  Basic basic_8 (.Cin(basic_7_cout), .X(in_15), .Y(in_16), .S(out_26));  // open: Cout
endmodule

module Basic (
  input  X,
  input  Y,
  input  Cin,
  output S,
  output Cout
);

  wire and_1_out, and_2_out, xor_1_out;

  and and_1 (and_1_out, Y, X);
  xor xor_1 (xor_1_out, Y, X);
  xor xor_2 (S, xor_1_out, Cin);
  and and_2 (and_2_out, xor_1_out, Cin);
  or or_1 (Cout, and_2_out, and_1_out);
endmodule
