// Logisim project 2to4decoder.circ as structural Verilog: 1 circuit, main circuit main
module main (
  input  I0,
  input  I1,
  output O0,
  output O1,
  output O2,
  output O3
);

  wire W, Y;

  not not_1 (Y, I0);
  not not_2 (W, I1);
  and and_1 (O0, I0, Y);
  and and_2 (O1, I1, W);
  and and_3 (O2, W, Y);
  and and_4 (O3, I0, I1);

  // Other names for the same wires on the sheet: X = I0; Z = I1
endmodule
