// Logisim project 3to8decoder.circ as structural Verilog: 1 circuit, main circuit main
module main (
  input  I0,
  input  I1,
  input  I2,
  output O0,
  output O4,
  output O1,
  output O5,
  output O2,
  output O6,
  output O3,
  output O7
);

  wire U, W, Y;

  not not_1 (Y, I0);
  not not_2 (W, I1);
  not not_3 (U, I2);
  and and_1 (O0, Y, W, U);
  and and_2 (O1, Y, W, I2);
  and and_3 (O2, Y, I1, U);
  and and_4 (O3, Y, I1, I2);
  and and_5 (O4, I0, W, U);
  and and_6 (O5, I0, W, I2);
  and and_7 (O6, I0, I1, U);
  and and_8 (O7, I0, I1, I2);

  // Other names for the same wires on the sheet: V = I2; X = I0; Z = I1
endmodule
