// Logisim project 8bit add sub.circ as structural Verilog: 1 circuit, main circuit main
module main (
  input  [7:0] in_1,
  input  [7:0] in_2,
  input  [7:0] in_3,
  input  [7:0] in_4,
  output [7:0] out_5,
  output out_6,
  output [7:0] out_7,
  output out_8
);

  Adder adder_1 (.a(in_1), .b(in_2), .out(out_5), .cin(1'b0), .cout(out_6));
  Subtractor subtractor_1 (.a(in_3), .b(in_4), .out(out_7), .bin(1'b0), .bout(out_8));
endmodule
