// Logisim project 8bit addsub scratch.circ as structural Verilog: 2 circuits, main circuit main
module main (
  input  in_1,
  input  in_2,
  input  in_3,
  input  in_4,
  input  in_5,
  input  in_6,
  input  in_7,
  input  in_8,
  input  [7:0] in_9,
  input  [7:0] in_10,
  output out_11,
  output out_12,
  output out_13,
  output out_14,
  output out_15,
  output [7:0] out_16,
  output out_17
);

  wire basic_1_s, basic_2_s, basic_3_s;

  Basic basic_1 (.Cin(1'b0), .X(in_1), .Y(in_2), .Cout(out_12), .S(basic_1_s));
  Basic basic_2 (.Cin(basic_1_s), .X(in_3), .Y(in_4), .Cout(out_13), .S(basic_2_s));
  Adder adder_1 (.a(in_9), .b(in_10), .out(out_16), .cin(1'b0), .cout(out_17));
  Basic basic_3 (.Cin(basic_2_s), .X(in_5), .Y(in_6), .Cout(out_14), .S(basic_3_s));
  Basic basic_4 (.Cin(basic_3_s), .X(in_7), .Y(in_8), .Cout(out_15), .S(out_11));
endmodule

module Basic (
  input  X,
  input  Y,
  input  Cin,
  output S,
  output Cout
);

  wire and_1_out, and_2_out, xor_1_out;

  and and_1 (and_1_out, Y, X);
  xor xor_1 (xor_1_out, Y, X);
  xor xor_2 (S, xor_1_out, Cin);
  and and_2 (and_2_out, xor_1_out, Cin);
  or or_1 (Cout, and_2_out, and_1_out);
endmodule
