// Logisim project JKff.circ as structural Verilog: 1 circuit, main circuit main
module main (
  output QAQB
);

  wire B_qn;

  J_K_Flip_Flop A (.J(QAQB), .K(QAQB), .preset(1'b0), .en(1'b0), .reset(1'b0));  // open: clk, Q, Qn
  J_K_Flip_Flop B (.J(B_qn), .K(QAQB), .Q(QAQB), .Qn(B_qn), .preset(1'b0), .en(1'b0), .reset(1'b0));  // open: clk
endmodule
