// Logisim project SRff.circ as structural Verilog: 1 circuit, main circuit main
module main (
  input  QA,
  input  QB
);

  wire and_1_out, s_r_ff_1_q, s_r_ff_1_qn, undriven, undriven_2;

  buf and_1 (and_1_out, undriven);  // AND_Gate
  S_R_Flip_Flop s_r_ff_1 (
    .S(and_1_out), .R(undriven_2), .Q(s_r_ff_1_q), .Qn(s_r_ff_1_qn), .preset(1'b0), .reset(1'b0));  // open: clk, en
endmodule
