// Logisim project Odd-Even-Counter.circ as structural Verilog: 1 circuit, main circuit main
module main (
  input  x
);

  wire _1a, _1b, _2a, _2b, _3a, _3b, _4a, Clock, Da, Db, Q_prime_a, Q_prime_b, Q_prime_c, Qa, Qb, Qc, x_prime;

  Clock clock_1 (.out(Clock));
  and and_1 (_1a, Qa, Q_prime_b);
  and and_2 (_1b, Q_prime_b, Qc);
  not not_1 (x_prime, x);
  and and_3 (_2a, x_prime, Q_prime_a, Qb);
  and and_4 (_2b, x_prime, Q_prime_b);
  D_Flip_Flop C (.clk(Clock), .D(x), .Q(Qc), .Qn(Q_prime_c));  // open: preset, en, reset
  and and_5 (_3a, Q_prime_a, Qb, Qc);
  and and_6 (_3b, x, Qb, Q_prime_c);
  D_Flip_Flop B (.clk(Clock), .D(Db), .Q(Qb), .Qn(Q_prime_b));  // open: preset, en, reset
  and and_7 (_4a, x, Qa, Qb, Q_prime_c);
  or or_1 (Db, _1b, _2b, _3b);
  or or_2 (Da, _1a, _2a, _3a, _4a);
  D_Flip_Flop A (.clk(Clock), .D(Da), .Q(Qa), .Qn(Q_prime_a));  // open: preset, en, reset
  Hex_Digit_Display hex_digit_display_1 (.value({1'b0, Qa, Qb, Qc}));  // open: dp

  // Other names for the same wires on the sheet: Dc = x
endmodule
