// Logisim project Up-Down-Counter.circ as structural Verilog: 1 circuit, main circuit main
module main (
  input  x
);

  wire _1a, _1b, _1c, _2a, _2b, _2c, _3a, _3b, _3c, _4a, _4b, _5a, Clock, Da, Db, Dc, Q_prime_a, Q_prime_b,
       Q_prime_c, Qa, Qb, Qc, x_prime;

  Clock clock_1 (.out(Clock));
  and and_1 (_1a, x, Q_prime_a, Q_prime_b, Q_prime_c);
  and and_2 (_1b, x, Q_prime_b, Q_prime_c);
  and and_3 (_1c, Q_prime_b, Q_prime_c);
  not not_1 (x_prime, x);
  and and_4 (_2a, x_prime, Q_prime_a, Qb, Qc);
  and and_5 (_2b, x_prime, Q_prime_b, Qc);
  and and_6 (_2c, Qa, Qb, Q_prime_c);
  D_Flip_Flop C (.clk(Clock), .D(Dc), .Q(Qc), .Qn(Q_prime_c));  // open: preset, en, reset
  and and_7 (_3a, x_prime, Qa, Q_prime_b);
  and and_8 (_3b, x, Qb, Qc);
  and and_9 (_3c, Q_prime_a, Q_prime_c);
  D_Flip_Flop B (.clk(Clock), .D(Db), .Q(Qb), .Qn(Q_prime_b));  // open: preset, en, reset
  and and_10 (_4a, x, Qa, Qc);
  and and_11 (_4b, x_prime, Qb, Q_prime_c);
  or or_1 (Dc, _1c, _2c, _3c);
  D_Flip_Flop A (.clk(Clock), .D(Da), .Q(Qa), .Qn(Q_prime_a));  // open: preset, en, reset
  and and_12 (_5a, Qa, Qb, Q_prime_c);
  or or_2 (Db, _1b, _2b, _3b, _4b);
  Hex_Digit_Display hex_digit_display_1 (.value({1'b0, Qa, Qb, Qc}));  // open: dp
  or or_3 (Da, _1a, _2a, _3a, _4a, _5a);
endmodule
