// Logisim project universal.circ as structural Verilog: 1 circuit, main circuit main
module main (
  input  x,
  input  [2:0] xyz,
  input  [1:0] xy,
  output [7:0] out_4,
  output [3:0] out_5,
  output [3:0] out_6
);

  wire clock_1_out, clock_2_out, clock_3_out, CLR_2_out, CLR_3_out, CLR_out, or_1_out;
  wire [1:0] counter_1_q, counter_2_q;
  wire [3:0] counter_3_q;
  wire [8:8] rom_3_data;

  Clock clock_1 (.out(clock_1_out));
  Button CLR (.out(CLR_out));
  Clock clock_2 (.out(clock_2_out));
  Button CLR_2 (.out(CLR_2_out));
  Counter #(.width(2), .max('h3)) counter_1 (
    .load(1'b0), .count(1'b1), .Q(counter_1_q), .clk(clock_1_out), .clr(CLR_out));  // open: D, carry
  Counter #(.width(2), .max('h3)) counter_2 (
    .load(1'b0), .count(1'b1), .Q(counter_2_q), .clk(clock_2_out), .clr(CLR_2_out));  // open: D, carry
  ROM #(.addrWidth(3), .dataWidth(4)) rom_1 (.addr({x, counter_1_q}), .data(out_5), .sel(1'b1));
  ROM #(.addrWidth(4), .dataWidth(4)) rom_2 (.addr({xy, counter_2_q}), .data(out_6), .sel(1'b1));
  Clock clock_3 (.out(clock_3_out));
  Button CLR_3 (.out(CLR_3_out));
  Counter #(.width(4), .max('hf)) counter_3 (
    .load(1'b0), .count(1'b1), .Q(counter_3_q), .clk(clock_3_out), .clr(or_1_out));  // open: D, carry
  or or_1 (or_1_out, CLR_3_out, rom_3_data[8]);
  ROM #(.addrWidth(7), .dataWidth(9)) rom_3 (.addr({xyz, counter_3_q}), .data({rom_3_data[8], out_4}), .sel(1'b1));

  // Notes on the sheet:
  //   contents of rom_1 (hex, n*v repeats v):
  //   0 2 4 6 1 3 5 7
  //   contents of rom_3 (hex, n*v repeats v):
  //   0 2 4 6 100 11*0 1 3 5 7 100 11*0 1 2 4 8 10 20 40 80 100 7*0 80 40 20 10 8 4 2 1 100 8*0 1 2 3 4 5
  //   6 7 8 9 a b c d e f f e d c b a 9 8 7 6 5 4 3 2 1
endmodule
